// Logisim project army_hard_coding_competition.circ as structural Verilog
module _4_bit_adder (
  input  in_1,
  input  in_2,
  input  in_3,
  input  in_4,
  input  in_5
);

  ExactlyOne xor_1 (.in0(in_5), .in1(in_4), .in2(in_3), .in3(in_2), .in4(in_1));  // open: out
endmodule
